# Fritzing sketch Schematic_Sensors (saved by Fritzing 0.9.3b)

parts:
  Mod1 = Raspberry Pi Pico
  OLED_I2C1 = OLED 128x64 I2C Monochrome Display  # not connected
  Mod2 = Full Size SD Card Module
  DS1 = DS18B20 1-Wire Temperature Sensor Probe
  Mod3 = KY-028 Digital Temperature Sensor Module [package="Breakout board"]
  Mod4 = KY-015 Temperature & Humidity Sensor Module [package="Breakout board"]
  GY1 = MPU-6050 Board GY-521 [form="♀ (female)" package=THT]
  Componente1 = AHT20 BMP280 pressure and humidity breakout
  Componente2 = BMP180 Breakout (GY-68)

nets:
  N1: Mod1.pin_4, DS1.DQ
  GND: Mod1.pin_8, Mod1.pin_13, Mod1.pin_23, Mod1.pin_38, Mod1.pin_42, Mod2.pin_15, DS1.GND, GY1.pin2, Componente2.GND
  N2: Mod1.pin_9, Mod4.S
  N3: Mod1.pin_14, Mod2.pin_11
  N4: Mod1.pin_15, Mod2.pin_9
  N5: Mod1.pin_16, Mod2.pin_13
  N6: Mod1.pin_17, Mod2.pin_7
  N7: Mod1.pin_21, Componente2.SDA
  N8: Mod1.pin_22, Componente2.SCL
  N9: Mod1.pin_24, GY1.pin4, Componente1.SDA
  N10: Mod1.pin_25, Componente1.SCL
  N11: Mod1.pin_34, Mod3.A0
  N12: Mod1.pin_36, GY1.pin1, Componente1.VDD

custom parts:
  Raspberry Pi Pico: Raspberry Pi Pico. Based around the RP2040 microcontroller the Pico is a low cost microcontroller device bringing Raspberry Pi quality, cost, and easy of use to the microcontroller space. Jan 2021, Split part in to two versions: tht (this one) and SMD. This one will drill holes for a .1 in header in pcb to allow plugging in the module as well as providing pads to solder the module to the top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
  Full Size SD Card Module: SD Card Module Slot Socket Reader For Arduino ARM MCU
  KY-028 Digital Temperature Sensor Module: KY-028 Digital Temperature Sensor Module, used to measure changes in temperature.
  KY-015 Temperature & Humidity Sensor Module: KY-015 temperature and humidity sensor module, provides a low-latency serial interface to measure humidity and temperature.
  MPU-6050 Board GY-521: Acelerometro y Giroscopio MPU-6050 Board GY-521
  AHT20 BMP280 pressure and humidity breakout: Cheap breakout board for the BMP280, barometric pressure sensor, and AHT20, humidity sensor
  BMP180 Breakout (GY-68): This is a simple breakout board for the BMP180, a high-precision, low-power barometric pressure sensor made by Bosch Sensortec. The range of measurement is from 300hPa to 1100hPa. The sensor can be supplied with voltage ranging from 1.8V to 3.6V. Operating temperature range is -40 to +85 °C. This particular breakout board (or perhaps the configuration) is produced by Shenzhen Keep Power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
