# Fritzing sketch Schematic_protoboard (saved by Fritzing 0.9.3b)
breadboards: 1

parts:
  OLED_I2C1 = OLED 128x64 I2C Monochrome Display
  Mod2 = Full Size SD Card Module
  Mod3 = KY-028 Digital Temperature Sensor Module [package="Breakout board"]
  Mod4 = KY-015 Temperature & Humidity Sensor Module [package="Breakout board"]
  GY1 = MPU-6050 Board GY-521 [form="♀ (female)" package=THT]
  Componente1 = AHT20 BMP280 pressure and humidity breakout
  Componente2 = BMP180 Breakout (GY-68)
  Mod5 = Raspberry Pi Pico
  DS2 = DS18B20 1-Wire Temperature Sensor Probe
  R1 = Resistor [tolerance=±5% resistance=220 package="0805 [SMD]"]

nets:
  VDD: OLED_I2C1.VDD, Mod2.pin_3, Mod2.pin_4, Mod3.+, Mod4.Vin, GY1.pin1, Componente1.VDD, Componente2.VCC, DS2.VDD, R1.Pin_0
  GND: OLED_I2C1.GND, Mod2.pin_1, Mod2.pin_16, Mod3.G, Mod4.-, GY1.pin2, Componente1.GND, Componente2.GND, DS2.GND
  N1: Mod2.pin_7, Mod5.pin_17
  N2: Mod2.pin_9, Mod5.pin_15
  N3: Mod2.pin_11, Mod5.pin_14
  N4: Mod2.pin_13, Mod5.pin_16
  N5: Mod3.A0, Mod5.pin_34
  N6: Mod4.S, Mod5.pin_9
  N7: Componente1.SCL, Mod5.pin_25
  N8: Componente1.SDA, Mod5.pin_24
  N9: Componente2.SCL, Mod5.pin_22
  N10: Componente2.SDA, Mod5.pin_21
  N11: Mod5.pin_3, Mod5.pin_8, Mod5.pin_13, Mod5.pin_18, Mod5.pin_23, Mod5.pin_28, Mod5.pin_33, Mod5.pin_38
  N12: Mod5.pin_4, DS2.DQ, R1.Pin_1

custom parts:
  Full Size SD Card Module: SD Card Module Slot Socket Reader For Arduino ARM MCU
  KY-028 Digital Temperature Sensor Module: KY-028 Digital Temperature Sensor Module, used to measure changes in temperature.
  KY-015 Temperature & Humidity Sensor Module: KY-015 temperature and humidity sensor module, provides a low-latency serial interface to measure humidity and temperature.
  MPU-6050 Board GY-521: Acelerometro y Giroscopio MPU-6050 Board GY-521
  AHT20 BMP280 pressure and humidity breakout: Cheap breakout board for the BMP280, barometric pressure sensor, and AHT20, humidity sensor
  BMP180 Breakout (GY-68): This is a simple breakout board for the BMP180, a high-precision, low-power barometric pressure sensor made by Bosch Sensortec. The range of measurement is from 300hPa to 1100hPa. The sensor can be supplied with voltage ranging from 1.8V to 3.6V. Operating temperature range is -40 to +85 °C. This particular breakout board (or perhaps the configuration) is produced by Shenzhen Keep Power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
  Raspberry Pi Pico: Raspberry Pi Pico. Based around the RP2040 microcontroller the Pico is a low cost microcontroller device bringing Raspberry Pi quality, cost, and easy of use to the microcontroller space. Jan 2021, Split part in to two versions: tht (this one) and SMD. This one will drill holes for a .1 in header in pcb to allow plugging in the module as well as providing pads to solder the module to the top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
